# Fritzing sketch dht22 sensor (saved by Fritzing 0.9.10b)

parts:
  U3 = ESP 32 DEVKIT DOIT
  DHT1 = DHT22 Humidity and Temperature Sensor

nets:
  N1: U3.D22, U3.D5, U3.3V3, DHT1.DATA
  VIN: U3.Vin, DHT1.VDD
  GND: U3.GND, DHT1.GND
