# Fritzing sketch flame sensor (saved by Fritzing 0.9.10b)

parts:
  U3 = ESP 32 DEVKIT DOIT
  Mod1 = KY-026 Flame Sensor Module [package="Breakout board"]

nets:
  N1: U3.D4, U3.3V3, Mod1.D0
  N2: U3.Vin, Mod1.+
  N3: U3.GND, Mod1.G

custom parts:
  KY-026 Flame Sensor Module: KY-026 Flame Sensor Module reacts in the presence of fire.
