# Fritzing sketch mq2 sensor (saved by Fritzing 0.9.10b)

parts:
  U3 = ESP 32 DEVKIT DOIT
  IC1 = MQ-2 [package="DIP (Dual Inline) [THT]"]

nets:
  N1: U3.Vin, IC1.pin1
  N2: U3.GND, IC1.pin2
  N3: U3.D32, IC1.pin4

custom parts:
  MQ-2: MQ-2 Gas Sensor module
