# Fritzing sketch water pump & buzzer (saved by Fritzing 0.9.10b)

parts:
  U3 = ESP 32 DEVKIT DOIT
  U4 = 2-Channel 5v Relay Shield [package=relay-2ch5v10a]
  JACK1 = 2.1mm Barrel Jack with Terminal Block
  WATER_PUMP1 = water pump/motor
  J1 = Piezo Speaker
  VALVE1 = Plastic Solenoid Valve  # not connected

nets:
  N1: U3.D19, U4.IN2
  N2: U3.D5, U3.TX2, U3.D15, U3.GND#13, J1.pin1, J1.pin2
  VIN: U3.Vin, U4.VCC
  N3: U3.GND#16, U4.GND
  N4: U4.K2-In, JACK1.POS
  N5: U4.K2-On, WATER_PUMP1.pin_2
  N6: JACK1.NEG, WATER_PUMP1.pin_1

custom parts:
  2-Channel 5v Relay Shield: 2 Channel 5v Relay Shield w. 2x SPD-06VDC-SD-C
  water pump/motor: WATER PUMP BY ARDUBLOCKTR
